# Fritzing sketch HandT (saved by Fritzing 0.9.3b)

parts:
  Adafruit_HUZZAH_ESP8266_Breakout1 = Adafruit HUZZAH ESP8266 Breakout [part_number=2471]
  RHT1 = Humidity and Temperature Sensor RHT03

nets:
  N1: Adafruit_HUZZAH_ESP8266_Breakout1.GND, RHT1.GND_1
  N2: Adafruit_HUZZAH_ESP8266_Breakout1.V+, RHT1.Vcc
  N3: Adafruit_HUZZAH_ESP8266_Breakout1.#13, RHT1.Data-signal

notes:
  Red = 5v
  Yellow = Data
  Black = Ground
  Data goes to a digital input pin.
  The sensore in this diagram is a RHT1 Temperature and Humidity sensor.
  The one that we have is the DHT11, is not the same model but its the same idea.
