# Fritzing sketch LightSensor (saved by Fritzing 0.9.3b)
breadboards: 1

parts:
  Adafruit_HUZZAH_ESP8266_Breakout1 = Adafruit HUZZAH ESP8266 Breakout [part_number=2471]
  R1 = Resistor [tolerance=±5% resistance=220 package="0603 [SMD]"]
  R2 = PHOTOCELL [package=photocell]
  LED1 = LED - 3mm [color="Red (633nm)" package="3 mm [THT]"]

nets (from the schematic view):
  N1: Adafruit_HUZZAH_ESP8266_Breakout1.GND, LED1.anode
  N2: Adafruit_HUZZAH_ESP8266_Breakout1.#16, R2.P$1
  N3: Adafruit_HUZZAH_ESP8266_Breakout1.A, R1.Pin_0
  N4: Adafruit_HUZZAH_ESP8266_Breakout1.V+, R2.P$2
  N5: R1.Pin_1, LED1.cathode
