# Fritzing sketch TempHumiditySensor (saved by Fritzing 0.9.3b)
breadboards: 1

parts:
  Componente1 = Arduino Mega 2560 (Rev3)
  RHT1 = Humidity and Temperature Sensor RHT03
  LCD1 = LCD screen
  R1 = Resistor [tolerance=±5% resistance=220 package="2010 [SMD]"]
  R2 = Trimmer Potentiometer [maximum_resistance=10kΩ package=THT]

nets:
  GND: Componente1.GND, RHT1.GND_2, LCD1.VSS, LCD1.R/W, LCD1.LED-, R2.leg1
  N1: Componente1.D12_PWM, LCD1.RS
  N2: Componente1.D11_PWM, LCD1.E
  5V: Componente1.5V, RHT1.GND_1, LCD1.VDD, R1.Pin_1, R2.leg2
  N3: Componente1.D2_PWM, LCD1.DB7
  N4: Componente1.D3_PWM, LCD1.DB6
  N5: Componente1.D4_PWM, LCD1.DB5
  N6: Componente1.D5_PWM, LCD1.DB4
  N7: Componente1.D7_PWM, RHT1.Data-signal
  N8: LCD1.V0, R2.wiper
  N9: LCD1.LED+, R1.Pin_0
