# Fritzing sketch TempSensor (saved by Fritzing 0.9.3b)
circuit board: 8.46667cm x 5.64444cm
breadboards: 1

parts:
  Componente1 = Arduino Uno (Rev3) - ICSP
  LED1 = 7-SEGMENT-4DIGIT-YOUNGSUN [package=7-segment-4digit-youngsun-longpads]
  U1 = TMP36 [package=to-92-kit]
  R1 = Resistor [tolerance=±5% resistance=220 package="2010 [SMD]"]
  R2 = Resistor [tolerance=±5% resistance=220 package="2010 [SMD]"]
  R3 = Resistor [tolerance=±5% resistance=220 package="2010 [SMD]"]
  R4 = Resistor [tolerance=±5% resistance=220 package="2010 [SMD]"]

nets (from the breadboard view):
  N1: Componente1.A0, U1.VOUT
  5V: Componente1.5V, U1.VCC
  GND: Componente1.GND, U1.GND
  N2: Componente1.D8, LED1.C
  N3: Componente1.D9_PWM, LED1.D
  N4: Componente1.D10_PWM/SS, LED1.E
  N5: Componente1.D11_PWM/MOSI, LED1.F
  N6: Componente1.D12/MISO, LED1.G
  N7: Componente1.D2, R1.Pin_0
  N8: Componente1.D3_PWM, R2.Pin_0
  N9: Componente1.D4, R3.Pin_1
  N10: Componente1.D5_PWM, R4.Pin_1
  N11: Componente1.D6_PWM, LED1.A
  N12: Componente1.D7, LED1.B
  N13: LED1.DIG1, R1.Pin_1
  N14: LED1.DIG2, R2.Pin_1
  N15: LED1.DIG3, R3.Pin_0
  N16: LED1.DIG4, R4.Pin_0
